# Fritzing sketch BreadBoard-fritzing (saved by Fritzing 0.9.4)
breadboards: 1

parts:
  IC1 = IC, DIP package, 40 pins [chip_label=ATMAGA-32A]
  LCD1 = LCD screen
  SW1 = DIP Switch 8 Position [package=dipswitch-08]
  R2 = Rotary Potentiometer (Large) [maximum_resistance=100kΩ package=THT]
  Power_plug2 = Power plug
  XTAL1 = Crystal [frequency="16 Mhz" package=THT]

nets:
  VDD: IC1.pin10, LCD1.VDD, LCD1.LED+, Power_plug2.VCC
  VSS: IC1.pin11, IC1.pin33, IC1.pin34, IC1.pin35, IC1.pin36, IC1.pin37, IC1.pin38, IC1.pin39, IC1.pin40, LCD1.VSS, LCD1.LED-, SW1.1, SW1.2, SW1.3, SW1.4, SW1.5, SW1.6, SW1.7, SW1.8, SW1.9, SW1.10, SW1.11, SW1.12, SW1.13, SW1.14, SW1.15, SW1.16, R2.leg2, Power_plug2.GND
  N1: IC1.pin12, XTAL1.pin_0
  N2: IC1.pin13, XTAL1.pin_1
  N3: IC1.pin22, LCD1.RS
  N4: IC1.pin23, LCD1.R/W
  N5: IC1.pin24, LCD1.E
  N6: IC1.pin26, LCD1.DB4
  N7: IC1.pin27, LCD1.DB5
  N8: IC1.pin28, LCD1.DB6
  N9: IC1.pin29, LCD1.DB7
  N10: LCD1.V0, R2.wiper

notes:
  PIN16 : LEDK
  PIN1 : VSS
  pin 1
  pin 40
  12 MHz
