# Fritzing sketch BreadBoard-fritzing (saved by Fritzing 0.9.4)
breadboards: 1

parts:
  GLCD_128x1 = 128 x 64 Graphic LCD
  IC1 = IC, DIP package, 40 pins [chip_label=ATMEGA-32]
  Power_plug1 = Power plug
  R1 = Rotary Potentiometer (Large) [maximum_resistance=100kΩ package=THT]
  Y1 = CRYSTAL [package=crystal-smd-5x3]

nets:
  N1: GLCD_128x1.1_Vss, GLCD_128x1.20_K(-), IC1.pin10, Power_plug1.GND, R1.leg1
  N2: GLCD_128x1.2_Vdd, GLCD_128x1.19_A(+), IC1.pin11, Power_plug1.VCC
  N3: GLCD_128x1.3_Vo, R1.wiper
  N4: GLCD_128x1.4_D/I, IC1.pin21
  N5: GLCD_128x1.5_R/W, IC1.pin20
  N6: GLCD_128x1.6_Enable, IC1.pin19
  N7: GLCD_128x1.7_DB0, IC1.pin22
  N8: GLCD_128x1.8_DB1, IC1.pin23
  N9: GLCD_128x1.9_BD2, IC1.pin24
  N10: GLCD_128x1.10_DB3, IC1.pin25
  N11: GLCD_128x1.11_DB4, IC1.pin26
  N12: GLCD_128x1.12_DB5, IC1.pin27
  N13: GLCD_128x1.13_DB6, IC1.pin28
  N14: GLCD_128x1.14_DB7, IC1.pin29
  N15: GLCD_128x1.15_CS1, IC1.pin18
  N16: GLCD_128x1.16_CS2, IC1.pin17
  N17: GLCD_128x1.17_RST, IC1.pin16
  N18: GLCD_128x1.18_Vout, R1.leg2
  N19: IC1.pin12, Y1.1
  N20: IC1.pin13, Y1.2
